// Logisim project ISA.circ as structural Verilog: 6 circuits, main circuit main
module main (
);

  wire and_1_out, B, Clk, FP, FS, FZ, MU, Sgn, WE, WM, Zero;
  wire [1:0] MP, MR;
  wire [2:0] OpULA;
  wire [23:0] bit_extender_1_out, rom_1_data;
  wire [31:0] bit_extender_3_out, IMM, JALR, multiplexer_1_out, multiplexer_2_out, multiplexer_3_out,
       multiplexer_4_out, multiplexer_5_out, PC_1, pc_1_pc_novo, PC_IMM, ram_1_dout,
       registerbank_1_readdata1, registerbank_1_readdata2;

  Multiplexer #(.width(32)) multiplexer_1 (.in0(PC_1), .in1(PC_IMM), .out(multiplexer_1_out), .sel(and_1_out));
  and and_1 (and_1_out, B, FZ);
  Multiplexer #(.select(2), .width(32)) multiplexer_2 (
    .in0(PC_1), .in1(multiplexer_1_out), .in2(PC_IMM), .in3(JALR), .out(multiplexer_2_out), .sel(MP));
  Multiplexer #(.width(32)) multiplexer_3 (
    .in0(multiplexer_2_out), .in1({32{1'b0}}), .out(multiplexer_3_out), .sel(FP));
  PCAdder pcadder_1 (.IMM(IMM), .PC(pc_1_pc_novo), .PCPlus1(PC_1), .PCPlusImm(PC_IMM));
  PC u_pc_1 (.PC_Ant(multiplexer_3_out), .Clk(Clk), .PC_Novo(pc_1_pc_novo));
  Bit_Extender #(.in_width(32), .out_width(24), .\type ("input")) bit_extender_1 (
    .in(pc_1_pc_novo), .out(bit_extender_1_out));  // open: extend
  ROM #(.addrWidth(24), .dataWidth(24)) rom_1 (.addr(bit_extender_1_out), .data(rom_1_data));
  Clock clock_1 (.out(Clk));
  assign IMM = {{24{rom_1_data[23]}}, rom_1_data[23:16]};  // Bit_Extender bit_extender_2
  RegisterBank registerbank_1 (
    .WE(WE), .WriteData(multiplexer_5_out), .RD(rom_1_data[15:12]), .Clk(Clk), .RS2(rom_1_data[11:8]),
    .RS1(rom_1_data[7:4]), .ReadData1(registerbank_1_readdata1), .ReadData2(registerbank_1_readdata2));
  ControlUnity controlunity_1 (
    .zero(Zero), .sinal(Sgn), .OpCode(rom_1_data[3:0]), .WE(WE), .MU(MU), .WM(WM), .MP(MP), .MR(MR), .FP(FP),
    .B(B), .FZ(FZ), .FS(FS), .OpULA(OpULA));
  Multiplexer #(.width(32)) multiplexer_4 (
    .in0(registerbank_1_readdata2), .in1(IMM), .out(multiplexer_4_out), .sel(MU));
  Multiplexer #(.select(2), .width(32)) multiplexer_5 (
    .in0(JALR), .in1(bit_extender_3_out), .in2(ram_1_dout), .in3(PC_1), .out(multiplexer_5_out), .sel(MR));
  ULA ula_1 (
    .Op2(multiplexer_4_out), .Op1(registerbank_1_readdata1), .Op_ULA(OpULA), .zero(Zero), .Resultado(JALR),
    .sinal(Sgn));
  Bit_Extender #(.in_width(1), .out_width(32), .\type ("input")) bit_extender_3 (
    .in(FS), .out(bit_extender_3_out));  // open: extend
  RAM #(.addrWidth(24), .dataWidth(32)) ram_1 (
    .addr(JALR[23:0]), .we(1'b1), .oe(WM), .clk(Clk), .din(registerbank_1_readdata2), .dout(ram_1_dout));

  // Notes on the sheet:
  //   contents of rom_1 (hex, n*v repeats v):
  //   57002 a8002 9870 a871 1b073 2c084 d875 e876 f877 9078 9879 a789 2087a bb002 2077a 2b002 fc6062 4076c
  //   906b 46062 41002 3500d 1110 f 7002 18002 29002 a010a a199 70a0a b780 7800 8b00 19092 a199 fa000d
  //   1b00 5e
endmodule

module ULA (
  input  [31:0] Op2,
  input  [31:0] Op1,
  input  [2:0] Op_ULA,
  output zero,
  output sinal,
  output [31:0] Resultado
);

  wire [31:0] adder_1_out, and_1_out, negator_1_out, or_1_out, shifter_1_out, shifter_2_out,
       subtractor_1_out, xor_1_out;

  Adder #(.width(32)) adder_1 (.a(Op1), .b(Op2), .out(adder_1_out));  // open: cin, cout
  Subtractor #(.width(32)) subtractor_1 (.a(Op1), .b(Op2), .out(subtractor_1_out), .bout(sinal));  // open: bin
  assign and_1_out = Op1 & Op2;  // AND_Gate and_1, 32 bits wide
  assign or_1_out = Op1 | Op2;  // OR_Gate or_1, 32 bits wide
  assign xor_1_out = Op1 ^ Op2;  // XOR_Gate xor_1, 32 bits wide
  Shifter #(.width(32)) shifter_1 (.in(Op1), .\dist (Op2[4:0]), .out(shifter_1_out));
  Shifter #(.shift("lr"), .width(32)) shifter_2 (.in(Op1), .\dist (Op2[4:0]), .out(shifter_2_out));
  Negator #(.width(32)) negator_1 (.in(Op1), .out(negator_1_out));
  Multiplexer #(.select(3), .width(32)) multiplexer_1 (
    .in0(adder_1_out), .in1(subtractor_1_out), .in2(and_1_out), .in3(or_1_out), .in4(xor_1_out),
    .in5(shifter_1_out), .in6(shifter_2_out), .in7(negator_1_out), .out(Resultado), .sel(Op_ULA));
  nor nor_1 (zero, subtractor_1_out[0], subtractor_1_out[1], subtractor_1_out[2], subtractor_1_out[3], subtractor_1_out[4], subtractor_1_out[5], subtractor_1_out[6], subtractor_1_out[7], subtractor_1_out[8], subtractor_1_out[9], subtractor_1_out[10], subtractor_1_out[11], subtractor_1_out[12], subtractor_1_out[13], subtractor_1_out[14], subtractor_1_out[15], subtractor_1_out[16], subtractor_1_out[17], subtractor_1_out[18], subtractor_1_out[19], subtractor_1_out[20], subtractor_1_out[21], subtractor_1_out[22], subtractor_1_out[23], subtractor_1_out[24], subtractor_1_out[25], subtractor_1_out[26], subtractor_1_out[27], subtractor_1_out[28], subtractor_1_out[29], subtractor_1_out[30], subtractor_1_out[31]);

  // Other names for the same wires on the sheet: sgn = sinal
endmodule

module RegisterBank (
  input  [31:0] WriteData,
  input  [3:0] RS1,
  input  WE,
  input  [3:0] RD,
  input  [3:0] RS2,
  input  Clk,
  output [31:0] ReadData1,
  output [31:0] ReadData2
);

  wire demultiplexer_1_out1, demultiplexer_1_out2, demultiplexer_1_out3, demultiplexer_1_out4,
       demultiplexer_1_out5, demultiplexer_1_out6, demultiplexer_1_out7, demultiplexer_1_out8,
       demultiplexer_1_out9, demultiplexer_1_out10, demultiplexer_1_out11, demultiplexer_1_out12,
       demultiplexer_1_out13, demultiplexer_1_out14, demultiplexer_1_out15;
  wire [31:0] r1_q, r2_q, r3_q, r4_q, r5_q, r6_q, r7_q, r8_q, r9_q, r10_q, r11_q, r12_q, r13_q, r14_q, r15_q;

  Demultiplexer #(.select(4)) demultiplexer_1 (
    .out1(demultiplexer_1_out1), .out2(demultiplexer_1_out2), .out3(demultiplexer_1_out3),
    .out4(demultiplexer_1_out4), .out5(demultiplexer_1_out5), .out6(demultiplexer_1_out6),
    .out7(demultiplexer_1_out7), .out8(demultiplexer_1_out8), .out9(demultiplexer_1_out9),
    .out10(demultiplexer_1_out10), .out11(demultiplexer_1_out11), .out12(demultiplexer_1_out12),
    .out13(demultiplexer_1_out13), .out14(demultiplexer_1_out14), .out15(demultiplexer_1_out15), .in(WE),
    .sel(RD));  // open: out0
  Register #(.width(32)) r1 (.D(WriteData), .en(demultiplexer_1_out1), .clk(Clk), .Q(r1_q));  // open: clr
  Register #(.width(32)) r2 (.D(WriteData), .en(demultiplexer_1_out2), .clk(Clk), .Q(r2_q));  // open: clr
  Register #(.width(32)) r3 (.D(WriteData), .en(demultiplexer_1_out3), .clk(Clk), .Q(r3_q));  // open: clr
  Register #(.width(32)) r4 (.D(WriteData), .en(demultiplexer_1_out4), .clk(Clk), .Q(r4_q));  // open: clr
  Register #(.width(32)) r5 (.D(WriteData), .en(demultiplexer_1_out5), .clk(Clk), .Q(r5_q));  // open: clr
  Register #(.width(32)) r6 (.D(WriteData), .en(demultiplexer_1_out6), .clk(Clk), .Q(r6_q));  // open: clr
  Register #(.width(32)) r7 (.D(WriteData), .en(demultiplexer_1_out7), .clk(Clk), .Q(r7_q));  // open: clr
  Register #(.width(32)) r8 (.D(WriteData), .en(demultiplexer_1_out8), .clk(Clk), .Q(r8_q));  // open: clr
  Register #(.width(32)) r9 (.D(WriteData), .en(demultiplexer_1_out9), .clk(Clk), .Q(r9_q));  // open: clr
  Register #(.width(32)) r10 (.D(WriteData), .en(demultiplexer_1_out10), .clk(Clk), .Q(r10_q));  // open: clr
  Register #(.width(32)) r11 (.D(WriteData), .en(demultiplexer_1_out11), .clk(Clk), .Q(r11_q));  // open: clr
  Register #(.width(32)) r12 (.D(WriteData), .en(demultiplexer_1_out12), .clk(Clk), .Q(r12_q));  // open: clr
  Register #(.width(32)) r13 (.D(WriteData), .en(demultiplexer_1_out13), .clk(Clk), .Q(r13_q));  // open: clr
  Register #(.width(32)) r14 (.D(WriteData), .en(demultiplexer_1_out14), .clk(Clk), .Q(r14_q));  // open: clr
  Register #(.width(32)) r15 (.D(WriteData), .en(demultiplexer_1_out15), .clk(Clk), .Q(r15_q));  // open: clr
  Multiplexer #(.select(4), .width(32)) multiplexer_1 (
    .in0({32{1'b0}}), .in1(r1_q), .in2(r2_q), .in3(r3_q), .in4(r4_q), .in5(r5_q), .in6(r6_q), .in7(r7_q),
    .in8(r8_q), .in9(r9_q), .in10(r10_q), .in11(r11_q), .in12(r12_q), .in13(r13_q), .in14(r14_q),
    .in15(r15_q), .out(ReadData1), .sel(RS1));
  Multiplexer #(.select(4), .width(32)) multiplexer_2 (
    .in0({32{1'b0}}), .in1(r1_q), .in2(r2_q), .in3(r3_q), .in4(r4_q), .in5(r5_q), .in6(r6_q), .in7(r7_q),
    .in8(r8_q), .in9(r9_q), .in10(r10_q), .in11(r11_q), .in12(r12_q), .in13(r13_q), .in14(r14_q),
    .in15(r15_q), .out(ReadData2), .sel(RS2));

  // Notes on the sheet:
  //   r0
endmodule

module PC (
  input  [31:0] PC_Ant,
  input  Clk,
  output [31:0] PC_Novo
);

  Register #(.width(32)) register_1 (.D(PC_Ant), .en(1'b1), .clk(Clk), .Q(PC_Novo));  // open: clr
endmodule

module ControlUnity (
  input  zero,
  input  sinal,
  input  [3:0] OpCode,
  output WE,
  output MU,
  output WM,
  output [1:0] MP,
  output [1:0] MR,
  output FP,
  output B,
  output FZ,
  output FS,
  output [2:0] OpULA
);

  wire and_1_out, and_2_out, and_3_out, and_4_out, and_5_out, and_6_out, and_9_out, and_10_out, and_11_out,
       and_12_out, and_13_out, and_14_out, and_15_out, and_16_out, and_17_out, and_18_out, and_19_out,
       and_20_out, and_21_out, and_22_out, and_23_out, and_24_out, and_25_out, and_26_out, and_28_out,
       and_29_out, not_1_out;

  not not_1 (not_1_out, OpCode[3]);
  and and_1 (and_1_out, OpCode[1], OpCode[2]);
  and and_2 (and_2_out, ~OpCode[1], ~OpCode[2]);  // AND_Gate
  and and_3 (and_3_out, OpCode[1], ~OpCode[2], ~OpCode[3]);  // AND_Gate
  and and_4 (and_4_out, ~OpCode[0], ~OpCode[1], OpCode[2]);  // AND_Gate
  and and_5 (and_5_out, OpCode[0], OpCode[1], OpCode[3]);
  and and_6 (and_6_out, OpCode[2], OpCode[3]);
  and and_7 (WM, ~OpCode[0], ~OpCode[1], OpCode[2], OpCode[3]);  // AND_Gate
  and and_8 (MP[0], ~OpCode[0], OpCode[1], OpCode[3]);  // AND_Gate
  and and_9 (and_9_out, OpCode[0], OpCode[2], OpCode[3]);
  and and_10 (and_10_out, OpCode[1], OpCode[2], OpCode[3]);
  and and_11 (and_11_out, OpCode[0], ~OpCode[1], OpCode[3]);  // AND_Gate
  and and_12 (and_12_out, OpCode[1], OpCode[2], OpCode[3]);
  and and_13 (and_13_out, OpCode[0], OpCode[1], OpCode[3]);
  and and_14 (and_14_out, OpCode[0], OpCode[2], OpCode[3]);
  and and_15 (and_15_out, OpCode[1], OpCode[2], OpCode[3]);
  and and_16 (and_16_out, ~OpCode[0], OpCode[1], OpCode[3]);  // AND_Gate
  and and_17 (and_17_out, OpCode[0], OpCode[2], OpCode[3]);
  and and_18 (and_18_out, ~OpCode[0], OpCode[1], OpCode[2], ~OpCode[3]);  // AND_Gate
  and and_19 (and_19_out, OpCode[0], ~OpCode[2], ~OpCode[3]);  // AND_Gate
  and and_20 (and_20_out, ~OpCode[0], ~OpCode[2], OpCode[3]);  // AND_Gate
  and and_21 (and_21_out, ~OpCode[0], OpCode[2], ~OpCode[3]);  // AND_Gate
  and and_22 (and_22_out, ~OpCode[0], ~OpCode[2], OpCode[3]);  // AND_Gate
  and and_23 (and_23_out, OpCode[0], ~OpCode[1], OpCode[2]);  // AND_Gate
  and and_24 (and_24_out, ~OpCode[0], ~OpCode[1], OpCode[2], ~OpCode[3]);  // AND_Gate
  and and_25 (and_25_out, ~OpCode[0], ~OpCode[2], OpCode[3]);  // AND_Gate
  and and_26 (and_26_out, OpCode[0], OpCode[1], ~OpCode[3]);  // AND_Gate
  Demultiplexer demultiplexer_1 (.out1(FZ), .in(zero), .sel(and_28_out));  // open: out0
  Demultiplexer demultiplexer_2 (.out1(FS), .in(sinal), .sel(and_29_out));  // open: out0
  or or_1 (WE, OpCode[0], not_1_out, and_1_out, and_2_out);
  or or_2 (MU, and_3_out, and_4_out, and_5_out, and_6_out);
  or or_3 (MP[1], and_9_out, and_10_out);
  or or_4 (MR[0], and_11_out, and_12_out);
  or or_5 (MR[1], and_13_out, and_14_out, and_15_out);
  and and_27 (FP, OpCode[0], OpCode[1], OpCode[2], OpCode[3]);
  or or_6 (B, and_16_out, and_17_out);
  and and_28 (and_28_out, ~OpCode[0], OpCode[1], ~OpCode[2], OpCode[3]);  // AND_Gate
  and and_29 (and_29_out, OpCode[0], ~OpCode[1], ~OpCode[2], OpCode[3]);  // AND_Gate
  or or_7 (OpULA[0], and_18_out, and_19_out, and_20_out);
  or or_8 (OpULA[1], and_21_out, and_22_out, and_23_out);
  or or_9 (OpULA[2], and_24_out, and_25_out, and_26_out);
endmodule

module PCAdder (
  input  [31:0] PC,
  input  [31:0] IMM,
  output [31:0] PCPlus1,
  output [31:0] PCPlusImm
);

  Adder #(.width(32)) adder_1 (.a(PC), .b(32'h1), .out(PCPlus1));  // open: cin, cout
  Adder #(.width(32)) adder_2 (.a(PC), .b(IMM), .out(PCPlusImm));  // open: cin, cout
endmodule
